# Fritzing sketch Boxes (saved by Fritzing 0.9.3b)
breadboards: 1

parts:
  Part1 = Arduino Due (Rev2b)
  LED-кнопка = LEDs [package=led10mm]
  НЛО = Header 2 [package=molex-1x2_lock]
  Кнопка_(Ниж_Бок_____Низ_Верх_Бок) = SWITCH_SPDT [package=kps-1290]
  Part2 = ws2812b [package="smd 2812b"]
  IC1 = ULN2803A [package=THT]

nets:
  5V: Part1.5V, Part2.VDD
  GND: Part1.GND, Кнопка_(Ниж_Бок_____Низ_Верх_Бок).P, Part2.VSS, IC1.0V
  N1: Part1.VIN, LED-кнопка.A, НЛО.1, IC1.COM_-_Common
  N2: Part1.D12_PWM, Part2.DIN
  N3: Part1.D30, Кнопка_(Ниж_Бок_____Низ_Верх_Бок).S
  N4: Part1.D31, IC1.In_1
  N5: LED-кнопка.C, IC1.Out_1
  N6: НЛО.2, Кнопка_(Ниж_Бок_____Низ_Верх_Бок).O

notes:
  +12V
  GND
